# Fritzing sketch arduino-temp-display (saved by Fritzing 0.9.3b)
breadboards: 1

parts:
  Part1 = Arduino Mega 2560 (Rev3)
  RHT1 = Humidity and Temperature Sensor RHT03
  LCD1 = LCD screen
  U1 = POT [package=alps_pot]

nets:
  N1: Part1.D12_PWM, LCD1.DB7
  N2: Part1.D11_PWM, LCD1.DB6
  N3: Part1.D10_PWM, LCD1.DB5
  N4: Part1.D9_PWM, LCD1.DB4
  N5: Part1.D8_PWM, LCD1.E
  N6: Part1.3V3, LCD1.LED+
  5V: Part1.5V, RHT1.GND_1, LCD1.VDD, U1.E
  GND: Part1.GND, RHT1.GND_2, LCD1.VSS, LCD1.R/W, LCD1.LED-, U1.A
  N7: Part1.D2_PWM, RHT1.Vcc
  N8: Part1.D7_PWM, LCD1.RS
  N9: LCD1.V0, U1.S
